# Fritzing sketch tide_wiring (saved by Fritzing 1.0.8)

parts:
  U1 = Tide Machine main board (rev B)
  M2 = 28BYJ-48 (DRUM)
  M3 = 28BYJ-48 (M2)
  M4 = 28BYJ-48 (O1)
  M5 = 28BYJ-48 (K1)
  M6 = 28BYJ-48 (N2)
  M7 = 28BYJ-48 (S2)
  H8 = Hall carrier (M2)
  H9 = Hall carrier (O1)
  H10 = Hall carrier (K1)
  H11 = Hall carrier (N2)
  H12 = Hall carrier (S2)
  CAL13 = Calendar carrier
  PS14 = 5 V 3 A supply

nets:
  N1: U1.J20.1_+3V3, CAL13.Y+
  N2: U1.J20.2_HALL_YEAR, CAL13.YS
  N3: U1.J20.3_GND, CAL13.Y-
  N4: U1.J21.1_+3V3, CAL13.M+
  N5: U1.J21.2_HALL_MOON, CAL13.MS
  N6: U1.J21.3_GND, CAL13.M-
  N7: U1.J5.1_CAL_Y1, CAL13.Y1
  N8: U1.J5.2_CAL_Y2, CAL13.Y2
  N9: U1.J5.3_CAL_Y3, CAL13.Y3
  N10: U1.J5.4_CAL_Y4, CAL13.Y4
  N11: U1.J5.5_CAL_M1, CAL13.M1
  N12: U1.J5.6_CAL_M2, CAL13.M2
  N13: U1.J5.7_CAL_M3, CAL13.M3
  N14: U1.J5.8_CAL_M4, CAL13.M4
  N15: U1.J22.1_+3V3, H8.+
  N16: U1.J22.2_HALL_M2, H8.S
  N17: U1.J22.3_GND, H8.-
  N18: U1.J23.1_+3V3, H9.+
  N19: U1.J23.2_HALL_O1, H9.S
  N20: U1.J23.3_GND, H9.-
  N21: U1.J24.1_+3V3, H10.+
  N22: U1.J24.2_HALL_K1, H10.S
  N23: U1.J24.3_GND, H10.-
  N24: U1.J25.1_+3V3, H11.+
  N25: U1.J25.2_HALL_N2, H11.S
  N26: U1.J25.3_GND, H11.-
  N27: U1.J26.1_+3V3, H12.+
  N28: U1.J26.2_HALL_S2, H12.S
  N29: U1.J26.3_GND, H12.-
  N30: U1.J3.1_VIN, PS14.+
  N31: U1.J3.2_GND, PS14.-
  N32: U1.J10.1_DRUM_A, M2.A
  N33: U1.J10.2_DRUM_B, M2.B
  N34: U1.J10.3_DRUM_C, M2.C
  N35: U1.J10.4_DRUM_D, M2.D
  N36: U1.J10.5_HOLD, M2.HOLD
  N37: U1.J11.1_M2_A, M3.A
  N38: U1.J11.2_M2_B, M3.B
  N39: U1.J11.3_M2_C, M3.C
  N40: U1.J11.4_M2_D, M3.D
  N41: U1.J11.5_HOLD, M3.HOLD
  N42: U1.J12.1_O1_A, M4.A
  N43: U1.J12.2_O1_B, M4.B
  N44: U1.J12.3_O1_C, M4.C
  N45: U1.J12.4_O1_D, M4.D
  N46: U1.J12.5_HOLD, M4.HOLD
  N47: U1.J13.1_K1_A, M5.A
  N48: U1.J13.2_K1_B, M5.B
  N49: U1.J13.3_K1_C, M5.C
  N50: U1.J13.4_K1_D, M5.D
  N51: U1.J13.5_HOLD, M5.HOLD
  N52: U1.J14.1_N2_A, M6.A
  N53: U1.J14.2_N2_B, M6.B
  N54: U1.J14.3_N2_C, M6.C
  N55: U1.J14.4_N2_D, M6.D
  N56: U1.J14.5_HOLD, M6.HOLD
  N57: U1.J15.1_S2_A, M7.A
  N58: U1.J15.2_S2_B, M7.B
  N59: U1.J15.3_S2_C, M7.C
  N60: U1.J15.4_S2_D, M7.D
  N61: U1.J15.5_HOLD, M7.HOLD

custom parts:
  Tide Machine main board (rev B): pcb/tide_main.kicad_pcb, 140 x 81.28 mm, drawn from the KiCad layout; the C6 shown fitted
  28BYJ-48 (DRUM): 5 V unipolar stepper, 64:1; leads blue, pink, yellow, orange, red
  28BYJ-48 (M2): 5 V unipolar stepper, 64:1; leads blue, pink, yellow, orange, red
  28BYJ-48 (O1): 5 V unipolar stepper, 64:1; leads blue, pink, yellow, orange, red
  28BYJ-48 (K1): 5 V unipolar stepper, 64:1; leads blue, pink, yellow, orange, red
  28BYJ-48 (N2): 5 V unipolar stepper, 64:1; leads blue, pink, yellow, orange, red
  28BYJ-48 (S2): 5 V unipolar stepper, 64:1; leads blue, pink, yellow, orange, red
  Hall carrier (M2): DRV5013 latch (TO-92) + 100 nF on perfboard; lead + S -
  Hall carrier (O1): DRV5013 latch (TO-92) + 100 nF on perfboard; lead + S -
  Hall carrier (K1): DRV5013 latch (TO-92) + 100 nF on perfboard; lead + S -
  Hall carrier (N2): DRV5013 latch (TO-92) + 100 nF on perfboard; lead + S -
  Hall carrier (S2): DRV5013 latch (TO-92) + 100 nF on perfboard; lead + S -
  Calendar carrier: BKA30D-R5 gauge stepper + year and moon latches on perfboard (outline: 4 x 6 corner cuts)
  5 V 3 A supply: MEAN WELL GST18U05-P1J or similar, centre positive
